# Fritzing sketch Cart-On_current (saved by Fritzing 0.9.3b)
breadboards: 1

parts:
  Raspberry_Pi_1 = Raspberry Pi 4 [part_number=RPI-4-b]
  M1 = BTS7960
  M4 = DC Motor
  M5 = BTS7960
  M6 = DC Motor
  U1 = TCM8240MD [package=tcm8240md]  # not connected
  M7 = RPlidar A1M8 [package=THT]  # not connected
  MIC1 = Microphone  # not connected
  J1 = Basic Servo
  J2 = Basic Servo

nets:
  N1: Raspberry_Pi_1.GPIO13, J1.pulse
  N2: Raspberry_Pi_1.GPIO19, J2.pulse
  GND: Raspberry_Pi_1.GPIO26, Raspberry_Pi_1.GND, M1.pin8, M5.pin8, J1.gnd, J2.gnd
  N3: Raspberry_Pi_1.GPIO20, M5.pin1
  N4: Raspberry_Pi_1.GPIO16, M1.pin1
  N5: Raspberry_Pi_1.GPIO12, M5.pin2
  N6: Raspberry_Pi_1.GPIO18, M1.pin2
  N7: Raspberry_Pi_1.5V, M1.pin7, M5.pin7
  N8: M1.pin9, M4.pin_2
  N9: M1.pin10, M4.pin_1
  VCC: M1.pin11, M5.pin11, J1.vcc, J2.vcc
  N10: M1.pin12, M5.pin12
  N11: M5.pin9, M6.pin_2
  N12: M5.pin10, M6.pin_1

custom parts:
  Raspberry Pi 4: The RPi4, a faster version of the awesome Raspberry Pi 2 B ARM Board with 40 pin gpio. Ready for special Raspberry Pi B+ and RPi2 Hat (Hardware attached (on) top)
  BTS7960: BTS7960 43A Peak Power H-Bridge PWM Motor Driver
  RPlidar A1M8: .The RPLIDAR A1 is the next generation low cost 360 degree 2D laser scanner (LIDAR) solution developed by SLAMTEC. It can take up to 4000 samples of laser ranging per second with high rotation speed. And equipped with SLAMTEC patented OPTMAG technology, it breakouts the life limitation of traditional LIDAR system so as to work stably for a long time.
